# Fritzing sketch circdigpotclose (saved by Fritzing 0.9.3b)
breadboards: 1

parts:
  R2 = Resistor [tolerance=±5% resistance=10k package=THT]
  R3 = Resistor [tolerance=±5% resistance=100 package=THT]

nets:
  N1: R2.Pin_1, R3.Pin_0

notes:
  RAW
  RWB
  Wiper
  A Terminal
  B Terminal
