# Fritzing sketch circhallcheck (saved by Fritzing 0.9.3b)
breadboards: 1

parts:
  U2 = HALL-EFFECT [part_number=US5881 package=sc70]
  Q1 = TRANSISTOR_NPN [package=to-92]
  R1 = Resistor [tolerance=±5% resistance=220 package=THT]
  LED1 = LED - 5mm [color="Red (633nm)" package="5 mm [THT]"]

nets:
  GND: U2.GND, Q1.E
  5V: U2.VCC, R1.Pin_0
  N1: U2.OUT, Q1.B
  N2: Q1.C, LED1.anode
  N3: R1.Pin_1, LED1.cathode

custom parts:
  HALL-EFFECT: Hall effect sensor in SC70 package
