# Fritzing sketch circspeedcontr (saved by Fritzing 0.9.3b)
breadboards: 1

parts:
  R1 = Resistor [tolerance=±5% resistance=100 package=THT]
  R2 = Resistor [tolerance=±5% resistance=100k package=THT]
  Q1 = TRANSISTOR_NPN [part_number=BD243C package=to-92-ammo]
  U2 = MCP41xxx [part_number=MCP4531 package=so08]
  V1 = DC Power [voltage=12V]
  Raspberry_Pi_1 = Raspberry Pi 3 [part_number=RPI-3-V1.2]
  M1 = DC Motor

nets:
  N1: R1.Pin_0, U2.A
  N2: R1.Pin_1, Q1.C, V1.V+
  GND: R2.Pin_0, U2.CS, U2.GND, V1.V-, Raspberry_Pi_1.GND, M1.pin_2
  N3: R2.Pin_1, U2.B
  N4: Q1.E, M1.pin_1
  N5: Q1.B, U2.W
  N6: U2.SCK, Raspberry_Pi_1.GPIO3
  N7: U2.DI, Raspberry_Pi_1.GPIO2
  VCC: U2.VCC, Raspberry_Pi_1.3V3

custom parts:
  MCP41xxx: SPI controlled single digital potentiometer by Microchip
