# Fritzing sketch circspeedcontr2 (saved by Fritzing 0.9.3b)
breadboards: 1

parts:
  R1 = Resistor [tolerance=±5% resistance=3.3k package=THT]
  R2 = Resistor [tolerance=±5% resistance=10k package=THT]
  Q1 = TRANSISTOR_NPN [part_number=BD243C package=to-92-ammo]
  Raspberry_Pi_1 = Raspberry Pi 3 [part_number=RPI-3-V1.2]
  M1 = DC Motor
  U4 = MCP41xxx [part_number=MCP4131 package=so08]
  R3 = Resistor [tolerance=±5% resistance=11k package=THT]
  U5 = LM 358 Dual Op-Amp [part_number=LM358 package="DIP8 [THT]"]
  V1 = DC Power [voltage=12V]

nets:
  N1: R1.Pin_1, U4.B
  N2: R2.Pin_0, Raspberry_Pi_1.GND, M1.pin_2
  N3: R2.Pin_1, R3.Pin_0, U5.connector1
  N4: Q1.E, M1.pin_1, R3.Pin_1
  N5: Q1.B, U5.connector0
  N6: Q1.C, U5.connector7, V1.V+
  N7: Raspberry_Pi_1.GPIO9, U4.DI
  N8: Raspberry_Pi_1.GPIO11, U4.SCK
  N9: Raspberry_Pi_1.GPIO8, U4.CS
  5V: Raspberry_Pi_1.5V, U4.A, U4.VCC
  N10: U4.W, U5.connector2
