# Fritzing sketch circspeedcontrclose (saved by Fritzing 0.9.3b)
breadboards: 1

parts:
  R1 = Rotary Potentiometer (Small) [maximum_resistance=10kΩ part_number=MCP4531 package=THT]
  R2 = Resistor [tolerance=±5% resistance=10k package=THT]
  R3 = Resistor [tolerance=±5% resistance=100 package=THT]

nets:
  N1: R1.leg1, R2.Pin_1
  N2: R1.leg2, R3.Pin_0
