# Fritzing sketch circspeeddetworkaround (saved by Fritzing 0.9.3b)
breadboards: 1

parts:
  Raspberry_Pi_1 = Raspberry Pi 3 [part_number=RPI-3-V1.2]
  U2 = HALL-EFFECT [part_number=US5881 package=sc70]
  U3 = MCP3424 [package=soic-14]

nets:
  N1: Raspberry_Pi_1.GPIO2, U3.BPDSW
  N2: Raspberry_Pi_1.GPIO3, U3.GND
  GND: Raspberry_Pi_1.GND, U2.GND, U3.DOUT, U3.AIN-
  5V: Raspberry_Pi_1.5V, U2.VCC, U3.GAIN, U3.REFIN-, U3.FILTER
  N3: U2.OUT, U3.SCLK

custom parts:
  HALL-EFFECT: Hall effect sensor in SC70 package
  MCP3424: 18bit ADC, I2C
